// Logisim project DFlipFlop.circ as structural Verilog: 2 circuits, main circuit main
module main (
);

  wire button_1_out, button_2_out, clock_1_out, clock_2_out, controlled_buffer_1_out, or_1_out,
       reg1b_1_outdata;
  wire [3:0] bit_extender_1_out;
  wire [7:0] adder_1_out, register_1_q;

  Button button_1 (.out(button_1_out));
  or or_1 (or_1_out, button_1_out, button_2_out);
  Clock clock_1 (.out(clock_1_out));
  Register register_1 (.D(adder_1_out), .en(1'b1), .clk(clock_2_out), .Q(register_1_q));  // open: clr
  Clock clock_2 (.out(clock_2_out));
  Button button_2 (.out(button_2_out));
  ROM rom_1 (.addr(register_1_q));  // open: data
  assign controlled_buffer_1_out = button_2_out ? 1'b1 : 1'bz;  // Controlled_Buffer controlled_buffer_1
  assign controlled_buffer_1_out = button_1_out ? 1'b0 : 1'bz;  // Controlled_Buffer controlled_buffer_2
  Adder adder_1 (.a(8'h1), .b(register_1_q), .out(adder_1_out));  // open: cin, cout
  Reg1B reg1b_1 (
    .Data(controlled_buffer_1_out), .Write(or_1_out), .Clock(clock_1_out), .OutData(reg1b_1_outdata));  // open: in_4, in_5, S, in_7, in_8, in_9, R, in_11, out_13, out_14, Result, out_16
  Hex_Digit_Display hex_digit_display_1 (.value(bit_extender_1_out));  // open: dp
  assign bit_extender_1_out = {{3{1'b0}}, reg1b_1_outdata};  // Bit_Extender bit_extender_1
endmodule

module Reg1B (
  input  Data,
  input  Write,
  input  Clock,
  input  in_4,
  input  in_5,
  input  S,
  input  in_7,
  input  in_8,
  input  in_9,
  input  R,
  input  in_11,
  output OutData,
  output out_13,
  output out_14,
  output Result,
  output out_16
);

  wire and_1_out, nand_1_out, nand_2_out, nand_4_out, nand_6_out, nand_9_out, nand_10_out, nand_12_out,
       not_1_out;

  and and_1 (and_1_out, Write, Clock);
  not not_1 (not_1_out, Data);
  nand nand_1 (nand_1_out, Data, and_1_out);
  nand nand_2 (nand_2_out, and_1_out, not_1_out);
  nand nand_3 (Result, S, nand_4_out);
  nand nand_4 (nand_4_out, Result, R);
  nand nand_5 (OutData, nand_1_out, nand_6_out);
  nand nand_6 (nand_6_out, OutData, nand_2_out);
  nand nand_7 (out_14, in_5, nand_9_out);
  nand nand_8 (out_16, in_7, nand_10_out);
  nand nand_9 (nand_9_out, out_14, in_9);
  nand nand_10 (nand_10_out, out_16, in_11);
  nand nand_11 (out_13, in_4, nand_12_out);
  nand nand_12 (nand_12_out, out_13, in_8);

  // Notes on the sheet:
  //   Data: pull=down
  //   Write: pull=down
  //   S-R Latch
  //   1 Bit register
  //   S-R Latch
  //   S-R Latch
  //   S-R Latch
endmodule
