// Logisim project NAND.circ as structural Verilog: 8 circuits, main circuit main
module main (
  output Carry,
  output Result
);

  wire and_1_out, and_2_out, decoder1b_1_out1, fulladder_1_carry, fulladder_2_carry, fulladder_3_carry,
       fulladder_4_carry, fulladder_4_result, halfadder_1_carry, halfadder_1_result, halfadder_2_carry,
       mux2to1_1_result, nand_1_out, nand_2_out, not_1_out, not_2_out, not_3_out, not_4_out, not_5_out,
       or_1_out, transistor_3_out, transistor_5_out, transistor_6_out, transistor_7_out, transistor_8_out,
       transistor_9_out, transistor_10_out, transistor_11_out, transistor_13_out, transistor_14_out,
       transistor_15_out, transistor_16_out, undriven;
  wire [3:0] fulladder_1_result;

  Transistor #(.\type ("n")) transistor_1 ();  // open: in, out, gate
  Transistor transistor_2 ();  // open: in, out, gate
  nand nand_1 (nand_1_out, 1'b1, 1'b1);
  not not_1 (not_1_out, 1'b0);
  not not_2 (not_2_out, 1'b0);
  Transistor transistor_3 (.in(1'b1), .out(transistor_3_out), .gate(1'b1));
  not not_3 (not_3_out, nand_1_out);
  nand nand_2 (nand_2_out, not_1_out, not_2_out);
  Transistor transistor_4 (.in(1'b1), .out(transistor_3_out), .gate(1'b0));
  Transistor #(.\type ("n")) transistor_5 (.in(transistor_3_out), .out(transistor_5_out), .gate(1'b1));
  Transistor #(.\type ("n")) transistor_6 (.in(transistor_5_out), .out(transistor_6_out), .gate(1'b0));
  Decoder1b decoder1b_1 (.Out1(decoder1b_1_out1));  // open: Sel, Out2
  Transistor transistor_7 (.in(1'b1), .out(transistor_7_out), .gate(1'b1));
  Transistor #(.\type ("n")) transistor_8 (.in(transistor_7_out), .out(transistor_8_out), .gate(1'b1));
  // Probe on transistor_7_out
  Pull_Resistor pull_resistor_1 (.node(transistor_7_out));
  not not_4 (not_4_out, 1'b0);
  not not_5 (not_5_out, 1'b1);
  FullAdder fulladder_1 (
    .Arg1(1'b1), .Arg2(1'b0), .Carry(fulladder_1_carry), .Result(fulladder_1_result[0]));  // open: Carry_in
  Pull_Resistor pull_resistor_2 (.node(transistor_3_out));
  and and_1 (and_1_out, 1'b1, not_4_out);
  and and_2 (and_2_out, not_5_out, 1'b0);
  Transistor transistor_9 (.in(1'b1), .out(transistor_9_out), .gate(1'b0));
  Transistor #(.\type ("n")) transistor_10 (.in(transistor_9_out), .out(transistor_10_out), .gate(1'b0));
  Mux2to1 mux2to1_1 (.in1(1'b0), .in2(1'b1), .result(mux2to1_1_result));  // open: Sel
  Transistor transistor_11 (.in(1'b1), .out(transistor_11_out), .gate(1'b1));
  // Probe on transistor_9_out
  Pull_Resistor pull_resistor_3 (.node(transistor_9_out));
  or or_1 (or_1_out, and_1_out, and_2_out);
  FullAdder fulladder_2 (
    .Arg1(1'b1), .Arg2(1'b0), .Carry_in(fulladder_1_carry), .Carry(fulladder_2_carry),
    .Result(fulladder_1_result[1]));
  Transistor transistor_12 (.in(1'b1), .out(transistor_11_out), .gate(1'b0));
  Transistor #(.\type ("n")) transistor_13 (.in(transistor_11_out), .out(transistor_13_out), .gate(1'b1));
  Transistor #(.\type ("n")) transistor_14 (.in(transistor_13_out), .out(transistor_14_out), .gate(1'b0));
  Pull_Resistor pull_resistor_4 (.node(transistor_11_out));
  // NOT_Gate not_6 is placed but not wired
  Transistor transistor_15 (.in(1'b1), .out(transistor_15_out), .gate(1'b1));
  Transistor #(.\type ("n")) transistor_16 (.in(transistor_15_out), .out(transistor_16_out), .gate(1'b1));
  Pull_Resistor pull_resistor_5 (.node(transistor_15_out));
  FullAdder fulladder_3 (
    .Arg1(1'b0), .Arg2(1'b0), .Carry_in(fulladder_2_carry), .Carry(fulladder_3_carry),
    .Result(fulladder_1_result[2]));
  FullAdder fulladder_4 (
    .Carry_in(undriven), .Carry(fulladder_4_carry), .Result(fulladder_4_result));  // open: Arg1, Arg2
  FullAdder fulladder_5 (
    .Arg1(1'b0), .Arg2(1'b1), .Carry_in(fulladder_3_carry), .Result(fulladder_1_result[3]));  // open: Carry
  Decoder1b decoder1b_2 ();  // open: Sel, Out1, Out2
  Decoder1b decoder1b_3 ();  // open: Sel, Out1, Out2
  HalfAdder halfadder_1 (.Arg1(1'b1), .Arg2(1'b1), .Carry(halfadder_1_carry), .Result(halfadder_1_result));
  // Probe on fulladder_1_result
  HalfAdder halfadder_2 (.Arg1(halfadder_1_result), .Arg2(1'b0), .Carry(halfadder_2_carry), .Result(Result));
  or or_2 (Carry, halfadder_1_carry, halfadder_2_carry);
  // also tied to GND on the sheet: {transistor_6_out, transistor_8_out, transistor_10_out, transistor_14_out, transistor_16_out}

  // Notes on the sheet:
  //   n-тип
  //   Исток
  //   Затвор
  //   Сток
  //   pmos1
  //   in1
  //   in2
  //   Транзистор
  //   p-тип
  //   Исток
  //   Затвор
  //   Сток
  //   AND
  //   OR
  //   in
  //   NAND
  //   +V
  //   pmos2
  //   nmos1
  //   nmos2
  //   GND
  //   +V
  //   pmos
  //   out
  //   nmos
  //   Gnd
  //   XOR
  //   out
  //   in
  //   pmos1
  //   in1
  //   in2
  //   +V
  //   pmos
  //   out
  //   nmos
  //   Gnd
  //   NAND
  //   +V
  //   pmos2
  //   nmos1
  //   nmos2
  //   GND
  //   in
  //   out
  //   +V
  //   pmos
  //   out
  //   nmos
  //   Gnd
endmodule

module HalfAdder (
  input  Arg1,
  input  Arg2,
  output Carry,
  output Result
);

  and and_1 (Carry, Arg2, Arg1);
  xor xor_1 (Result, Arg1, Arg2);
endmodule

module FullAdder (
  input  Arg1,
  input  Arg2,
  input  Carry_in,
  output Carry,
  output Result
);

  wire halfadder_1_carry, halfadder_1_result, halfadder_2_carry;

  HalfAdder halfadder_1 (.Arg1(Arg1), .Arg2(Arg2), .Carry(halfadder_1_carry), .Result(halfadder_1_result));
  HalfAdder halfadder_2 (.Arg1(halfadder_1_result), .Arg2(Carry_in), .Carry(halfadder_2_carry), .Result(Result));
  or or_1 (Carry, halfadder_1_carry, halfadder_2_carry);
endmodule

module Mux2to1 (
  input  in1,
  input  Sel,
  input  in2,
  output result
);

  wire nand_1_out, nand_2_out, not_1_out;

  not not_1 (not_1_out, Sel);
  nand nand_1 (nand_1_out, in1, not_1_out);
  nand nand_2 (nand_2_out, Sel, in2);
  nand nand_3 (result, nand_1_out, nand_2_out);
endmodule

module mux4to1 (
  input  in1,
  input  in2,
  input  [1:0] sel,
  output result
);

  wire mux2to1_1_result, mux2to1_2_result;

  Mux2to1 mux2to1_1 (.in1(in1), .Sel(sel[0]), .in2(in2), .result(mux2to1_1_result));
  Mux2to1 mux2to1_2 (.in1(in1), .Sel(sel[0]), .in2(in2), .result(mux2to1_2_result));
  Mux2to1 mux2to1_3 (.in1(mux2to1_1_result), .Sel(sel[1]), .in2(mux2to1_2_result), .result(result));
endmodule

module Decoder1b (
  input  Sel,
  output Out1,
  output Out2
);

  wire not_1_out;

  not not_1 (not_1_out, Sel);
  assign Out1 = not_1_out ? 1'b1 : 1'bz;  // Controlled_Buffer controlled_buffer_1
  assign Out2 = Sel ? 1'b1 : 1'bz;  // Controlled_Buffer controlled_buffer_2
  Controlled_Buffer controlled_buffer_3 ();  // open: in, out, en
  Pull_Resistor pull_resistor_1 (.node(Out1));
  Pull_Resistor pull_resistor_2 (.node(Out2));

  // Notes on the sheet:
  //   Out1: pull=down
  //   Out2: pull=down
  //   Decoder1B
  //   in
  //   Controlled buffer(Switch)
  //   out
  //   Enable
endmodule

module Decoder2B (
);

  wire controlled_buffer_1_out, controlled_buffer_2_out, controlled_buffer_3_out, controlled_buffer_4_out,
       decoder1b_1_out1, decoder1b_1_out2, decoder1b_2_out1, decoder1b_2_out2, not_1_out;

  assign controlled_buffer_1_out = not_1_out ? decoder1b_1_out1 : 1'bz;  // Controlled_Buffer controlled_buffer_1
  Decoder1b decoder1b_1 (.Sel(1'b1), .Out1(decoder1b_1_out1), .Out2(decoder1b_1_out2));
  assign controlled_buffer_2_out = not_1_out ? decoder1b_1_out2 : 1'bz;  // Controlled_Buffer controlled_buffer_2
  not not_1 (not_1_out, 1'b1);
  assign controlled_buffer_3_out = 1'b1 ? decoder1b_2_out1 : 1'bz;  // Controlled_Buffer controlled_buffer_3
  Decoder1b decoder1b_2 (.Sel(1'b1), .Out1(decoder1b_2_out1), .Out2(decoder1b_2_out2));
  assign controlled_buffer_4_out = 1'b1 ? decoder1b_2_out2 : 1'bz;  // Controlled_Buffer controlled_buffer_4
  Pull_Resistor pull_resistor_1 (.node(controlled_buffer_1_out));
  Pull_Resistor pull_resistor_2 (.node(controlled_buffer_2_out));
  Pull_Resistor pull_resistor_3 (.node(controlled_buffer_3_out));
  Pull_Resistor pull_resistor_4 (.node(controlled_buffer_4_out));
endmodule

module Negat (
  input  [7:0] in_1
);

  wire [7:0] adder_2_out, adder_3_out, adder_4_out, not_1_out, not_2_out;

  Adder adder_1 ();  // open: a, b, out, cin, cout
  assign not_1_out = ~in_1;  // NOT_Gate not_1, 8 bits wide
  Adder adder_2 (.a(not_1_out), .b(8'h1), .out(adder_2_out));  // open: cin, cout
  assign not_2_out = ~8'h2;  // NOT_Gate not_2, 8 bits wide
  Adder adder_3 (.a(not_2_out), .b(8'h1), .out(adder_3_out));  // open: cin, cout
  Adder adder_4 (.a(8'h8), .b(adder_3_out), .out(adder_4_out));  // open: cin, cout
  // Probe on adder_4_out

  // Notes on the sheet:
  //   Arg1
  //   Arg2
  //   Сумматор
  //   Negator
  //   Result
  //   Вычисление разности
endmodule
