// Logisim project SPC32.circ as structural Verilog: 13 circuits, main circuit main
module main (
);

  wire cpu_1_read, cpu_1_write, gpu_1_drawing, gpu_1_reset, rgb_video_1_p2;
  wire [3:0] button_4_out, gpu_1_drawdata_2, gpu_1_drawdata_3;
  wire [23:0] gpu_1_drawdata;
  wire [31:0] cpu_1_address, cpu_1_writedata, memory_1_out_data;

  CPU cpu_1 (
    .ReadData(memory_1_out_data), .Address(cpu_1_address), .WriteData(cpu_1_writedata), .Write(cpu_1_write),
    .Read(cpu_1_read));
  Memory memory_1 (
    .ADRESS(cpu_1_address), .WRITE(cpu_1_write), .READ(cpu_1_read), .IN_DATA(cpu_1_writedata),
    .OUT_DATA(memory_1_out_data));
  GPU gpu_1 (
    .Read(cpu_1_read), .Address(cpu_1_address), .Data(cpu_1_writedata), .Write(cpu_1_write),
    .OutData(memory_1_out_data), .DrawData({gpu_1_drawdata_3, gpu_1_drawdata_2, gpu_1_drawdata}),
    .Reset(gpu_1_reset), .Drawing(gpu_1_drawing));
  InputOutput inputoutput_1 (
    .Keyboard(button_4_out), .Address(cpu_1_address), .Read(cpu_1_read), .Drawing(gpu_1_drawing),
    .OutData(memory_1_out_data));
  // RGB_Video #(.height(16), .scale(8), .width(16)) rgb_video_1: pin names not known; wires that end beside it: gpu_1_reset, rgb_video_1_p2, rgb_video_1_p2, gpu_1_drawdata_3, gpu_1_drawdata_2, gpu_1_drawdata
  Clock clock_1 (.out(rgb_video_1_p2));
  Button button_1 (.out(button_4_out[2]));
  Button button_2 (.out(button_4_out[3]));
  Button button_3 (.out(button_4_out[1]));
  Button button_4 (.out(button_4_out[0]));
endmodule

module ProgramCounter (
  input  [31:0] InputAddress,
  input  FETCH,
  input  Load,
  output [31:0] OutputAddress,
  output ReadMem,
  output [31:0] PC
);

  wire clock_1_out, clock_2_out;
  wire [31:0] adder_1_out, multiplexer_1_out, register_1_q;

  Clock clock_1 (.out(clock_1_out));
  Multiplexer #(.width(32)) multiplexer_1 (.in0(adder_1_out), .in1(InputAddress), .out(multiplexer_1_out), .sel(Load));
  Register #(.width(32)) register_1 (
    .D(multiplexer_1_out), .en(FETCH), .clk(clock_1_out), .Q(register_1_q));  // open: clr
  assign OutputAddress = FETCH ? register_1_q : 32'bz;  // Controlled_Buffer controlled_buffer_1
  Adder #(.width(32)) adder_1 (.a(32'h4), .b(register_1_q), .out(adder_1_out));  // open: cin, cout
  Register #(.width(32)) register_2 (.D(register_1_q), .en(clock_2_out), .clk(clock_2_out), .Q(PC));  // open: clr
  Clock clock_2 (.out(clock_2_out));

  assign ReadMem = FETCH;

  // Notes on the sheet:
  //   Load: pull=down
endmodule

module InstrDecoder (
  input  [31:0] INSTR,
  input  FETCH,
  input  Decode,
  input  [2:0] IMM_TYPE,
  output [6:0] OPCODE,
  output [4:0] RD,
  output [2:0] funct3,
  output [4:0] RS1,
  output [4:0] RS2,
  output [6:0] funct7,
  output [31:0] IMMEDIATE
);

  wire clock_1_out;
  wire [31:0] bit_extender_1_out, bit_extender_2_out, bit_extender_3_out, register_1_q;

  Clock clock_1 (.out(clock_1_out));
  Register #(.width(32)) register_1 (.D(INSTR), .en(FETCH), .clk(clock_1_out), .Q(register_1_q));  // open: clr
  assign {funct7, RS2, RS1, funct3, RD, OPCODE} = Decode ? register_1_q : 32'bz;  // Controlled_Buffer controlled_buffer_1
  assign bit_extender_1_out = {{20{funct7[6]}}, {funct7, RS2}};  // Bit_Extender bit_extender_1
  assign bit_extender_2_out = {{20{funct7[6]}}, {funct7, RD}};  // Bit_Extender bit_extender_2
  assign bit_extender_3_out = {{19{funct7[6]}}, {funct7[6], RD[0], funct7[5:0], RD[4:1], 1'b0}};  // Bit_Extender bit_extender_3
  Multiplexer #(.select(3), .width(32)) multiplexer_1 (
    .in1(bit_extender_1_out), .in2(bit_extender_2_out), .in3(bit_extender_3_out),
    .in4({funct7, RS2, RS1, funct3, {12{1'b0}}}),
    .in5({{11{1'b0}}, funct7[6], RS1, funct3, RS2[0], funct7[5:0], RS2[4:1], 1'b0}), .out(IMMEDIATE),
    .sel(IMM_TYPE));  // open: in0, in6, in7

  // Notes on the sheet:
  //   I-TYPE IMMEDIATE
  //   S-TYPE IMMEDIATE
  //   B-TYPE IMMEDIATE
  //   U-TYPE IMMEDIATE
  //   J-TYPE IMMEDIATE
endmodule

module Memory (
  input  [31:0] ADRESS,
  input  WRITE,
  input  READ,
  input  [31:0] IN_DATA,
  output [31:0] OUT_DATA
);

  wire and_1_out, and_2_out, clock_1_out, not_1_out, or_1_out;
  wire [31:0] ram_1_dout;

  not not_1 (not_1_out, ADRESS[18]);
  // Probe on ADRESS[17:2]
  and and_1 (and_1_out, not_1_out, WRITE);
  and and_2 (and_2_out, not_1_out, READ);
  RAM #(.addrWidth(16), .asyncread("true"), .dataWidth(32), .\type ("nonvolatile")) ram_1 (
    .addr(ADRESS[17:2]), .we(and_1_out), .oe(and_2_out), .clk(clock_1_out), .din(IN_DATA), .dout(ram_1_dout));
  Clock clock_1 (.out(clock_1_out));
  or or_1 (or_1_out, and_1_out, and_2_out);
  assign OUT_DATA = or_1_out ? ram_1_dout : 32'bz;  // Controlled_Buffer controlled_buffer_1

  // Notes on the sheet:
  //   OUT_DATA: pull=down
  //   WRITE: pull=down
  //   READ: pull=down
endmodule

module OpcodeDecoder (
  input  [6:0] OPCODE,
  output ERROR,
  output StoreMem,
  output LoadMem,
  output IMMEDIATE,
  output [2:0] IMM_TYPE,
  output WriteReg,
  output Fetch,
  output Decode,
  output Branch,
  output JAL,
  output JALR,
  output LUI,
  output AUIPC
);

  wire clock_1_out, d_ff_1_q, decoder_1_out12, nor_1_out, not_1_out, not_2_out, or_1_out, or_2_out;

  not not_1 (not_1_out, ERROR);
  nand nand_1 (ERROR, OPCODE[0], OPCODE[1]);
  Decoder #(.select(5)) decoder_1 (
    .out0(LoadMem), .out4(IMMEDIATE), .out5(AUIPC), .out8(StoreMem), .out12(decoder_1_out12), .out13(LUI),
    .out24(Branch), .out25(JALR), .out27(JAL), .sel(OPCODE[6:2]), .en(not_1_out));  // open: out1, out2, out3, out6, out7, out9, out10, out11, out14, out15, out16, out17, out18, out19, out20, out21, out22, out23, out26, out28, out29, out30, out31
  or or_1 (or_1_out, IMMEDIATE, JALR, LoadMem);
  assign IMM_TYPE = or_1_out ? 3'b001 : 3'bz;  // Controlled_Buffer controlled_buffer_1
  assign IMM_TYPE = StoreMem ? 3'b010 : 3'bz;  // Controlled_Buffer controlled_buffer_2
  or or_2 (or_2_out, LUI, AUIPC);
  assign IMM_TYPE = Branch ? 3'b011 : 3'bz;  // Controlled_Buffer controlled_buffer_3
  assign IMM_TYPE = or_2_out ? 3'b100 : 3'bz;  // Controlled_Buffer controlled_buffer_4
  assign IMM_TYPE = JAL ? 3'b101 : 3'bz;  // Controlled_Buffer controlled_buffer_5
  or or_3 (WriteReg, 1'b0, decoder_1_out12, IMMEDIATE, LoadMem, JAL, LUI, AUIPC);
  nor nor_1 (nor_1_out, LoadMem, StoreMem);
  not not_2 (not_2_out, nor_1_out);
  Clock clock_1 (.out(clock_1_out));
  or or_4 (Fetch, nor_1_out, d_ff_1_q);
  D_Flip_Flop d_ff_1 (.D(not_2_out), .clk(clock_1_out), .Q(d_ff_1_q));  // open: Qn, preset, reset
  D_Flip_Flop d_ff_2 (.D(Fetch), .clk(clock_1_out), .Q(Decode));  // open: Qn, preset, reset

  // Notes on the sheet:
  //   StoreMem: pull=down
  //   LoadMem: pull=down
endmodule

module RegisterFile (
  input  [31:0] DATA,
  input  [4:0] RS1,
  input  [4:0] RS2,
  input  [4:0] RD,
  input  WRITE,
  output [31:0] OUT1,
  output [31:0] OUT2
);

  wire decoder_1_out0, decoder_1_out1, decoder_1_out2, decoder_1_out3;
  wire [31:0] registerbank8_1_out1, registerbank8_1_out2, registerbank8_2_out1, registerbank8_2_out2,
       registerbank8_3_out1, registerbank8_3_out2, registerbank8zero_1_out1, registerbank8zero_1_out2;

  Decoder #(.select(2)) decoder_1 (
    .out0(decoder_1_out0), .out1(decoder_1_out1), .out2(decoder_1_out2), .out3(decoder_1_out3),
    .sel(RD[4:3]), .en(WRITE));
  RegisterBank8Zero registerbank8zero_1 (
    .RS1(RS1[2:0]), .RS2(RS2[2:0]), .DATA(DATA), .WRITE(decoder_1_out0), .RD(RD[2:0]),
    .OUT1(registerbank8zero_1_out1), .OUT2(registerbank8zero_1_out2));
  RegisterBank8 registerbank8_1 (
    .RS1(RS1[2:0]), .RS2(RS2[2:0]), .DATA(DATA), .WRITE(decoder_1_out1), .RD(RD[2:0]),
    .OUT1(registerbank8_1_out1), .OUT2(registerbank8_1_out2));
  RegisterBank8 registerbank8_2 (
    .RS1(RS1[2:0]), .RS2(RS2[2:0]), .DATA(DATA), .WRITE(decoder_1_out2), .RD(RD[2:0]),
    .OUT1(registerbank8_2_out1), .OUT2(registerbank8_2_out2));
  RegisterBank8 registerbank8_3 (
    .RS1(RS1[2:0]), .RS2(RS2[2:0]), .DATA(DATA), .WRITE(decoder_1_out3), .RD(RD[2:0]),
    .OUT1(registerbank8_3_out1), .OUT2(registerbank8_3_out2));
  Multiplexer #(.select(2), .width(32)) multiplexer_1 (
    .in0(registerbank8zero_1_out1), .in1(registerbank8_1_out1), .in2(registerbank8_2_out1),
    .in3(registerbank8_3_out1), .out(OUT1), .sel(RS1[4:3]));
  Multiplexer #(.select(2), .width(32)) multiplexer_2 (
    .in0(registerbank8zero_1_out2), .in1(registerbank8_1_out2), .in2(registerbank8_2_out2),
    .in3(registerbank8_3_out2), .out(OUT2), .sel(RS2[4:3]));
endmodule

module RegisterBank8 (
  input  [2:0] RS1,
  input  [2:0] RS2,
  input  [31:0] DATA,
  input  WRITE,
  input  [2:0] RD,
  output [31:0] OUT1,
  output [31:0] OUT2
);

  wire clock_1_out, decoder_1_out0, decoder_1_out1, decoder_1_out2, decoder_1_out3, decoder_1_out4,
       decoder_1_out5, decoder_1_out6, decoder_1_out7;
  wire [31:0] register_1_q, register_2_q, register_3_q, register_4_q, register_5_q, register_6_q,
       register_7_q, register_8_q;

  Clock clock_1 (.out(clock_1_out));
  Decoder #(.select(3)) decoder_1 (
    .out0(decoder_1_out0), .out1(decoder_1_out1), .out2(decoder_1_out2), .out3(decoder_1_out3),
    .out4(decoder_1_out4), .out5(decoder_1_out5), .out6(decoder_1_out6), .out7(decoder_1_out7), .sel(RD),
    .en(WRITE));
  Register #(.width(32)) register_1 (.D(DATA), .en(decoder_1_out0), .clk(clock_1_out), .Q(register_1_q));  // open: clr
  Register #(.width(32)) register_2 (.D(DATA), .en(decoder_1_out1), .clk(clock_1_out), .Q(register_2_q));  // open: clr
  Register #(.width(32)) register_3 (.D(DATA), .en(decoder_1_out2), .clk(clock_1_out), .Q(register_3_q));  // open: clr
  Register #(.width(32)) register_4 (.D(DATA), .en(decoder_1_out3), .clk(clock_1_out), .Q(register_4_q));  // open: clr
  Register #(.width(32)) register_5 (.D(DATA), .en(decoder_1_out4), .clk(clock_1_out), .Q(register_5_q));  // open: clr
  Register #(.width(32)) register_6 (.D(DATA), .en(decoder_1_out5), .clk(clock_1_out), .Q(register_6_q));  // open: clr
  Register #(.width(32)) register_7 (.D(DATA), .en(decoder_1_out6), .clk(clock_1_out), .Q(register_7_q));  // open: clr
  Register #(.width(32)) register_8 (.D(DATA), .en(decoder_1_out7), .clk(clock_1_out), .Q(register_8_q));  // open: clr
  Multiplexer #(.select(3), .width(32)) multiplexer_1 (
    .in0(register_1_q), .in1(register_2_q), .in2(register_3_q), .in3(register_4_q), .in4(register_5_q),
    .in5(register_6_q), .in6(register_7_q), .in7(register_8_q), .out(OUT1), .sel(RS1));
  Multiplexer #(.select(3), .width(32)) multiplexer_2 (
    .in0(register_1_q), .in1(register_2_q), .in2(register_3_q), .in3(register_4_q), .in4(register_5_q),
    .in5(register_6_q), .in6(register_7_q), .in7(register_8_q), .out(OUT2), .sel(RS2));
endmodule

module RegisterBank8Zero (
  input  [2:0] RS1,
  input  [2:0] RS2,
  input  [31:0] DATA,
  input  WRITE,
  input  [2:0] RD,
  output [31:0] OUT1,
  output [31:0] OUT2
);

  wire clock_1_out, decoder_1_out0, decoder_1_out1, decoder_1_out2, decoder_1_out3, decoder_1_out4,
       decoder_1_out5, decoder_1_out6, decoder_1_out7;
  wire [31:0] register_1_q, register_2_q, register_3_q, register_4_q, register_5_q, TEST1_q, TEST2_q, ZERO_q;

  Clock clock_1 (.out(clock_1_out));
  Decoder #(.select(3)) decoder_1 (
    .out0(decoder_1_out0), .out1(decoder_1_out1), .out2(decoder_1_out2), .out3(decoder_1_out3),
    .out4(decoder_1_out4), .out5(decoder_1_out5), .out6(decoder_1_out6), .out7(decoder_1_out7), .sel(RD),
    .en(WRITE));
  Register #(.width(32)) ZERO (.D({32{1'b0}}), .en(decoder_1_out0), .clk(clock_1_out), .Q(ZERO_q));  // open: clr
  Register #(.width(32)) TEST1 (.D(DATA), .en(decoder_1_out1), .clk(clock_1_out), .Q(TEST1_q));  // open: clr
  Register #(.width(32)) TEST2 (.D(DATA), .en(decoder_1_out2), .clk(clock_1_out), .Q(TEST2_q));  // open: clr
  Register #(.width(32)) register_1 (.D(DATA), .en(decoder_1_out3), .clk(clock_1_out), .Q(register_1_q));  // open: clr
  Register #(.width(32)) register_2 (.D(DATA), .en(decoder_1_out4), .clk(clock_1_out), .Q(register_2_q));  // open: clr
  Register #(.width(32)) register_3 (.D(DATA), .en(decoder_1_out5), .clk(clock_1_out), .Q(register_3_q));  // open: clr
  Register #(.width(32)) register_4 (.D(DATA), .en(decoder_1_out6), .clk(clock_1_out), .Q(register_4_q));  // open: clr
  Register #(.width(32)) register_5 (.D(DATA), .en(decoder_1_out7), .clk(clock_1_out), .Q(register_5_q));  // open: clr
  Multiplexer #(.select(3), .width(32)) multiplexer_1 (
    .in0(ZERO_q), .in1(TEST1_q), .in2(TEST2_q), .in3(register_1_q), .in4(register_2_q), .in5(register_3_q),
    .in6(register_4_q), .in7(register_5_q), .out(OUT1), .sel(RS1));
  Multiplexer #(.select(3), .width(32)) multiplexer_2 (
    .in0(ZERO_q), .in1(TEST1_q), .in2(TEST2_q), .in3(register_1_q), .in4(register_2_q), .in5(register_3_q),
    .in6(register_4_q), .in7(register_5_q), .out(OUT2), .sel(RS2));
endmodule

module ALU32 (
  input  IMM,
  input  [6:0] Funct7,
  input  [31:0] ARG1,
  input  [2:0] Funct3,
  input  [31:0] ARG2,
  output [31:0] Result
);

  wire and_2_out, comparator_1_lt, comparator_2_lt, not_1_out;
  wire [31:0] adder_1_out, and_1_out, bit_extender_1_out, bit_extender_2_out, multiplexer_1_out,
       multiplexer_2_out, or_1_out, shifter_1_out, shifter_2_out, shifter_3_out, subtractor_1_out, xor_1_out;

  Adder #(.width(32)) adder_1 (.a(ARG1), .b(ARG2), .out(adder_1_out));  // open: cin, cout
  Subtractor #(.width(32)) subtractor_1 (.a(ARG1), .b(ARG2), .out(subtractor_1_out));  // open: bin, bout
  Shifter #(.width(32)) shifter_1 (.in(ARG1), .\dist (ARG2[4:0]), .out(shifter_1_out));
  Comparator #(.width(32)) comparator_1 (.a(ARG1), .b(ARG2), .lt(comparator_1_lt));  // open: gt, eq
  Comparator #(.mode("unsigned"), .width(32)) comparator_2 (.a(ARG1), .b(ARG2), .lt(comparator_2_lt));  // open: gt, eq
  Shifter #(.shift("lr"), .width(32)) shifter_2 (.in(ARG1), .\dist (ARG2[4:0]), .out(shifter_2_out));
  Shifter #(.shift("ar"), .width(32)) shifter_3 (.in(ARG1), .\dist (ARG2[4:0]), .out(shifter_3_out));
  assign bit_extender_1_out = {{31{1'b0}}, comparator_1_lt};  // Bit_Extender bit_extender_1
  assign bit_extender_2_out = {{31{1'b0}}, comparator_2_lt};  // Bit_Extender bit_extender_2
  assign xor_1_out = ARG1 ^ ARG2;  // XOR_Gate xor_1, 32 bits wide
  assign or_1_out = ARG1 | ARG2;  // OR_Gate or_1, 32 bits wide
  assign and_1_out = ARG1 & ARG2;  // AND_Gate and_1, 32 bits wide
  not not_1 (not_1_out, IMM);
  and and_2 (and_2_out, not_1_out, Funct7[5]);
  Multiplexer #(.width(32)) multiplexer_1 (
    .in0(adder_1_out), .in1(subtractor_1_out), .out(multiplexer_1_out), .sel(and_2_out));
  Multiplexer #(.width(32)) multiplexer_2 (
    .in0(shifter_2_out), .in1(shifter_3_out), .out(multiplexer_2_out), .sel(Funct7[5]));
  Multiplexer #(.select(3), .width(32)) multiplexer_3 (
    .in0(multiplexer_1_out), .in1(shifter_1_out), .in2(bit_extender_1_out), .in3(bit_extender_2_out),
    .in4(xor_1_out), .in5(multiplexer_2_out), .in6(or_1_out), .in7(and_1_out), .out(Result), .sel(Funct3));
endmodule

module Branch (
  input  [31:0] ARG1,
  input  [2:0] Funct3,
  input  [31:0] ARG2,
  input  Enable,
  output Result
);

  wire comparator_1_eq, comparator_2_eq, comparator_3_lt, comparator_4_eq, comparator_4_gt, comparator_5_lt,
       comparator_6_eq, comparator_6_gt, not_1_out, or_1_out, or_2_out;

  Comparator #(.width(32)) comparator_1 (.a(ARG1), .b(ARG2), .eq(comparator_1_eq));  // open: gt, lt
  Comparator #(.width(32)) comparator_2 (.a(ARG1), .b(ARG2), .eq(comparator_2_eq));  // open: gt, lt
  Comparator #(.width(32)) comparator_3 (.a(ARG1), .b(ARG2), .lt(comparator_3_lt));  // open: gt, eq
  Comparator #(.width(32)) comparator_4 (.a(ARG1), .b(ARG2), .gt(comparator_4_gt), .eq(comparator_4_eq));  // open: lt
  Comparator #(.mode("unsigned"), .width(32)) comparator_5 (.a(ARG1), .b(ARG2), .lt(comparator_5_lt));  // open: gt, eq
  Comparator #(.mode("unsigned"), .width(32)) comparator_6 (
    .a(ARG1), .b(ARG2), .gt(comparator_6_gt), .eq(comparator_6_eq));  // open: lt
  not not_1 (not_1_out, comparator_2_eq);
  or or_1 (or_1_out, comparator_4_gt, comparator_4_eq);
  or or_2 (or_2_out, comparator_6_gt, comparator_6_eq);
  Multiplexer #(.enable("true"), .select(3)) multiplexer_1 (
    .in0(comparator_1_eq), .in1(not_1_out), .in4(comparator_3_lt), .in5(or_1_out), .in6(comparator_5_lt),
    .in7(or_2_out), .out(Result), .sel(Funct3), .en(Enable));  // open: in2, in3
endmodule

module CPU (
  input  [31:0] ReadData,
  output [31:0] Address,
  output [31:0] WriteData,
  output Write,
  output Read
);

  wire branch_1_result, not_1_out, opcodedecoder_1_auipc, opcodedecoder_1_branch, opcodedecoder_1_decode,
       opcodedecoder_1_error, opcodedecoder_1_fetch, opcodedecoder_1_immediate, opcodedecoder_1_jal,
       opcodedecoder_1_jalr, opcodedecoder_1_loadmem, opcodedecoder_1_lui, opcodedecoder_1_writereg,
       or_1_out, or_3_out, or_4_out, programcounter_1_readmem;
  wire [2:0] instrdecoder_1_funct3, opcodedecoder_1_imm_type;
  wire [4:0] instrdecoder_1_rd, instrdecoder_1_rs1, instrdecoder_1_rs2;
  wire [6:0] instrdecoder_1_funct7, instrdecoder_1_opcode;
  wire [31:0] adder_1_out, adder_2_out, adder_3_out, alu32_1_result, instrdecoder_1_immediate,
       multiplexer_1_out, multiplexer_2_out, multiplexer_3_out, multiplexer_4_out, multiplexer_5_out,
       multiplexer_6_out, multiplexer_7_out, programcounter_1_pc, registerfile_1_out1;

  Multiplexer #(.width(32)) multiplexer_1 (
    .in0(programcounter_1_pc), .in1(registerfile_1_out1), .out(multiplexer_1_out), .sel(opcodedecoder_1_jalr));
  ProgramCounter programcounter_1 (
    .InputAddress(adder_1_out), .FETCH(opcodedecoder_1_fetch), .Load(or_3_out), .OutputAddress(Address),
    .ReadMem(programcounter_1_readmem), .PC(programcounter_1_pc));
  Adder #(.width(32)) adder_1 (
    .a(multiplexer_1_out), .b(instrdecoder_1_immediate), .out(adder_1_out));  // open: cin, cout
  Adder #(.width(32)) adder_2 (
    .a(registerfile_1_out1), .b(instrdecoder_1_immediate), .out(adder_2_out));  // open: cin, cout
  assign Address = or_1_out ? adder_2_out : 32'bz;  // Controlled_Buffer controlled_buffer_1
  or or_1 (or_1_out, Write, opcodedecoder_1_loadmem);
  or or_2 (Read, programcounter_1_readmem, opcodedecoder_1_loadmem);
  Multiplexer #(.width(32)) multiplexer_2 (.in0(ReadData), .in1({32{1'b0}}), .out(multiplexer_2_out), .sel(or_3_out));
  InstrDecoder instrdecoder_1 (
    .INSTR(multiplexer_2_out), .FETCH(opcodedecoder_1_fetch), .Decode(opcodedecoder_1_decode),
    .IMM_TYPE(opcodedecoder_1_imm_type), .OPCODE(instrdecoder_1_opcode), .RD(instrdecoder_1_rd),
    .funct3(instrdecoder_1_funct3), .RS1(instrdecoder_1_rs1), .RS2(instrdecoder_1_rs2),
    .funct7(instrdecoder_1_funct7), .IMMEDIATE(instrdecoder_1_immediate));
  or or_3 (or_3_out, opcodedecoder_1_jalr, opcodedecoder_1_jal, branch_1_result);
  OpcodeDecoder opcodedecoder_1 (
    .OPCODE(instrdecoder_1_opcode), .ERROR(opcodedecoder_1_error), .StoreMem(Write),
    .LoadMem(opcodedecoder_1_loadmem), .IMMEDIATE(opcodedecoder_1_immediate),
    .IMM_TYPE(opcodedecoder_1_imm_type), .WriteReg(opcodedecoder_1_writereg), .Fetch(opcodedecoder_1_fetch),
    .Decode(opcodedecoder_1_decode), .Branch(opcodedecoder_1_branch), .JAL(opcodedecoder_1_jal),
    .JALR(opcodedecoder_1_jalr), .LUI(opcodedecoder_1_lui), .AUIPC(opcodedecoder_1_auipc));
  Branch branch_1 (
    .ARG1(registerfile_1_out1), .Funct3(instrdecoder_1_funct3), .ARG2(WriteData),
    .Enable(opcodedecoder_1_branch), .Result(branch_1_result));
  Adder #(.width(32)) adder_3 (
    .a(programcounter_1_pc), .b(instrdecoder_1_immediate), .out(adder_3_out));  // open: cin, cout
  Multiplexer #(.width(32)) multiplexer_3 (
    .in0(instrdecoder_1_immediate), .in1(multiplexer_6_out), .out(multiplexer_3_out), .sel(not_1_out));
  not not_1 (not_1_out, opcodedecoder_1_lui);
  or or_4 (or_4_out, opcodedecoder_1_jal, opcodedecoder_1_jalr);
  Multiplexer #(.width(32)) multiplexer_4 (
    .in0(alu32_1_result), .in1(ReadData), .out(multiplexer_4_out), .sel(opcodedecoder_1_loadmem));
  Multiplexer #(.width(32)) multiplexer_5 (
    .in0(multiplexer_3_out), .in1(adder_3_out), .out(multiplexer_5_out), .sel(opcodedecoder_1_auipc));
  Multiplexer #(.width(32)) multiplexer_6 (
    .in0(multiplexer_4_out), .in1(Address), .out(multiplexer_6_out), .sel(or_4_out));
  RegisterFile registerfile_1 (
    .DATA(multiplexer_5_out), .RS1(instrdecoder_1_rs1), .RS2(instrdecoder_1_rs2), .RD(instrdecoder_1_rd),
    .WRITE(opcodedecoder_1_writereg), .OUT1(registerfile_1_out1), .OUT2(WriteData));
  Multiplexer #(.width(32)) multiplexer_7 (
    .in0(WriteData), .in1(instrdecoder_1_immediate), .out(multiplexer_7_out), .sel(opcodedecoder_1_immediate));
  ALU32 alu32_1 (
    .IMM(opcodedecoder_1_immediate), .Funct7(instrdecoder_1_funct7), .ARG1(registerfile_1_out1),
    .Funct3(instrdecoder_1_funct3), .ARG2(multiplexer_7_out), .Result(alu32_1_result));

  // Notes on the sheet:
  //   PC INPUT
  //   PC OUTPUT
  //   MemoryOut
  //   InstrDecoder Out
  //   OPCODE DECODER
  //   DATA
endmodule

module GPU (
  input  Read,
  input  [31:0] Address,
  input  [31:0] Data,
  input  Write,
  output [31:0] OutData,
  output [31:0] DrawData,
  output Reset,
  output Drawing
);

  wire and_1_out, and_2_out, and_3_out, and_4_out, and_6_out, clock_1_out, clock_2_out, clock_3_out,
       clock_4_out, comparator_1_eq, comparator_2_eq, multiplexer_1_out, not_1_out, not_2_out, not_3_out,
       or_1_out;
  wire [7:0] counter_1_q, multiplexer_2_out, register_1_q;
  wire [31:0] ram_1_dout;

  and and_1 (and_1_out, Address[18], Read, not_1_out);
  not not_1 (not_1_out, Address[19]);
  and and_2 (and_2_out, Address[18], not_2_out, not_3_out);
  not not_2 (not_2_out, Drawing);
  not not_3 (not_3_out, comparator_1_eq);
  Comparator #(.width(32)) comparator_1 (.a(Data), .b({32{1'b1}}), .eq(comparator_1_eq));  // open: gt, lt
  Register register_1 (.D(Address[9:2]), .en(and_2_out), .clk(clock_1_out), .Q(register_1_q));  // open: clr
  Clock clock_1 (.out(clock_1_out));
  and and_3 (and_3_out, not_3_out, and_4_out);
  and and_4 (and_4_out, Address[18], Write);
  Clock clock_2 (.out(clock_2_out));
  and and_5 (Reset, and_4_out, comparator_1_eq);
  T_Flip_Flop t_ff_1 (.T(multiplexer_1_out), .clk(clock_3_out), .Q(Drawing));  // open: Qn, reset, preset
  Multiplexer multiplexer_1 (.in0(Reset), .in1(comparator_2_eq), .out(multiplexer_1_out), .sel(Drawing));
  Clock clock_3 (.out(clock_3_out));
  Comparator comparator_2 (.a(register_1_q), .b(counter_1_q), .eq(comparator_2_eq));  // open: gt, lt
  and and_6 (and_6_out, Drawing, comparator_2_eq);
  Clock clock_4 (.out(clock_4_out));
  Counter counter_1 (
    .load(and_6_out), .count(Drawing), .clk(clock_4_out), .D({8{1'b0}}), .Q(counter_1_q));  // open: clr, up, carry
  or or_1 (or_1_out, and_1_out, Drawing);
  Multiplexer #(.width(8)) multiplexer_2 (
    .in0(Address[9:2]), .in1(counter_1_q), .out(multiplexer_2_out), .sel(Drawing));
  RAM #(.asyncread("true"), .clearpin("true"), .dataWidth(32)) ram_1 (
    .addr(multiplexer_2_out), .we(and_3_out), .oe(or_1_out), .clk(clock_2_out), .din(Data), .dout(ram_1_dout));  // open: clr
  assign OutData = and_1_out ? ram_1_dout : 32'bz;  // Controlled_Buffer controlled_buffer_1
  assign DrawData = Drawing ? ram_1_dout : 32'bz;  // Controlled_Buffer controlled_buffer_2

  // Notes on the sheet:
  //   dont draw last ffffff
  //   Toggle when stopped draw
  //   Drawing
endmodule

module InputOutput (
  input  [3:0] Keyboard,
  input  [31:0] Address,
  input  Read,
  input  Drawing,
  output [31:0] OutData
);

  wire and_1_out, clock_1_out, comparator_1_gt;
  wire [31:0] bit_extender_1_out, bit_extender_2_out, multiplexer_1_out, register_1_q;

  and and_1 (and_1_out, Address[18], Read, Address[19]);
  assign bit_extender_1_out = {{28{1'b0}}, Keyboard};  // Bit_Extender bit_extender_1
  Register #(.width(32)) register_1 (
    .D(bit_extender_1_out), .en(comparator_1_gt), .clk(clock_1_out), .Q(register_1_q));  // open: clr
  Clock clock_1 (.out(clock_1_out));
  Comparator #(.mode("unsigned"), .width(4)) comparator_1 (
    .a(Keyboard), .b(4'b0000), .gt(comparator_1_gt));  // open: eq, lt
  Multiplexer #(.enable("true"), .width(32)) multiplexer_1 (
    .in0(register_1_q), .in1(bit_extender_2_out), .out(multiplexer_1_out), .sel(Address[2]), .en(and_1_out));
  assign bit_extender_2_out = {{31{1'b0}}, Drawing};  // Bit_Extender bit_extender_2
  assign OutData = and_1_out ? multiplexer_1_out : 32'bz;  // Controlled_Buffer controlled_buffer_1
endmodule
