// Logisim project SPC8S.circ as structural Verilog: 6 circuits, main circuit main
module main (
);

  wire clock_1_out, conditions_1_jmp, instrdecoder_1_alu_active, instrdecoder_1_conditional,
       instrdecoder_1_loadmem, instrdecoder_1_read, instrdecoder_1_storemem, instrdecoder_1_write;
  wire [1:0] instrdecoder_1_opcode;
  wire [2:0] instrdecoder_1_readaddr, instrdecoder_1_writeaddr;
  wire [3:0] instrdecoder_1_const;
  wire [7:0] alu8_1_result, instrdecoder_1_jmpadress, multiplexer_1_out, multiplexer_2_out,
       programcounter_1_outputdata, ram_1_dout, registerbank_1_arg0, registerbank_1_arg1,
       registerbank_1_arg2, registerbank_1_outputdata, registerbank_1_ramadress;

  ProgramCounter programcounter_1 (
    .Load(conditions_1_jmp), .Data(instrdecoder_1_jmpadress), .OutputData(programcounter_1_outputdata));
  // Probe on programcounter_1_outputdata
  InstrDecoder instrdecoder_1 (
    .INSTR(programcounter_1_outputdata), .Write(instrdecoder_1_write), .WriteAddr(instrdecoder_1_writeaddr),
    .Read(instrdecoder_1_read), .ReadAddr(instrdecoder_1_readaddr), .Const(instrdecoder_1_const),
    .OPCODE(instrdecoder_1_opcode), .ALU_ACTIVE(instrdecoder_1_alu_active),
    .Conditional(instrdecoder_1_conditional), .JmpAdress(instrdecoder_1_jmpadress),
    .LoadMem(instrdecoder_1_loadmem), .StoreMem(instrdecoder_1_storemem));
  Multiplexer #(.width(8)) multiplexer_1 (
    .in0(alu8_1_result), .in1(multiplexer_2_out), .out(multiplexer_1_out), .sel(instrdecoder_1_read));
  RegisterBank registerbank_1 (
    .WriteReg(instrdecoder_1_writeaddr), .WRITE(instrdecoder_1_write), .READ(instrdecoder_1_read),
    .InputData(multiplexer_1_out), .ReadReg(instrdecoder_1_readaddr), .OutputData(registerbank_1_outputdata),
    .ARG0(registerbank_1_arg0), .ARG1(registerbank_1_arg1), .ARG2(registerbank_1_arg2),
    .RamAdress(registerbank_1_ramadress));
  ALU8 alu8_1 (
    .ARG1(registerbank_1_arg1), .ARG2(registerbank_1_arg2), .OPCODE(instrdecoder_1_opcode),
    .Const(instrdecoder_1_const), .ACTIVE(instrdecoder_1_alu_active), .RESULT(alu8_1_result));
  Multiplexer #(.width(8)) multiplexer_2 (
    .in0(registerbank_1_outputdata), .in1(ram_1_dout), .out(multiplexer_2_out), .sel(instrdecoder_1_loadmem));
  // Probe on registerbank_1_outputdata
  Clock clock_1 (.out(clock_1_out));
  RAM #(.enables("line")) ram_1 (
    .addr(registerbank_1_ramadress), .we(instrdecoder_1_storemem), .clk(clock_1_out),
    .din(registerbank_1_outputdata), .dout(ram_1_dout));
  Conditions conditions_1 (.ACTIVE(instrdecoder_1_conditional), .REG0(registerbank_1_arg0), .JMP(conditions_1_jmp));
endmodule

module Conditions (
  input  ACTIVE,
  input  [7:0] REG0,
  output JMP
);

  wire comparator_1_eq;

  Comparator comparator_1 (.a(REG0), .b({8{1'b0}}), .eq(comparator_1_eq));  // open: gt, lt
  assign JMP = ACTIVE ? comparator_1_eq : 1'bz;  // Controlled_Buffer controlled_buffer_1
endmodule

module ALU8 (
  input  [7:0] ARG1,
  input  [7:0] ARG2,
  input  [1:0] OPCODE,
  input  [3:0] Const,
  input  ACTIVE,
  output [7:0] RESULT
);

  wire [7:0] adder_1_out, bit_extender_1_out, multiplexer_1_out, nand_1_out, subtractor_1_out, xor_1_out;

  assign nand_1_out = ~(ARG1 & ARG2);  // NAND_Gate nand_1, 8 bits wide
  assign xor_1_out = ARG1 ^ ARG2;  // XOR_Gate xor_1, 8 bits wide
  Subtractor subtractor_1 (.a(ARG1), .b(ARG2), .out(subtractor_1_out));  // open: bin, bout
  Adder adder_1 (.a(ARG1), .b(ARG2), .out(adder_1_out));  // open: cin, cout
  Multiplexer #(.enable("true"), .select(2), .width(8)) multiplexer_1 (
    .in0(adder_1_out), .in1(subtractor_1_out), .in2(xor_1_out), .in3(nand_1_out), .out(multiplexer_1_out),
    .sel(OPCODE), .en(ACTIVE));
  Adder adder_2 (.a(multiplexer_1_out), .b(bit_extender_1_out), .out(RESULT));  // open: cin, cout
  assign bit_extender_1_out = {{4{1'b0}}, Const};  // Bit_Extender bit_extender_1
  Conditions conditions_1 ();  // open: ACTIVE, REG0, JMP
endmodule

module RegisterBank (
  input  [2:0] WriteReg,
  input  WRITE,
  input  READ,
  input  [7:0] InputData,
  input  [2:0] ReadReg,
  output [7:0] OutputData,
  output [7:0] ARG0,
  output [7:0] ARG1,
  output [7:0] ARG2,
  output [7:0] RamAdress
);

  wire CLOCK_GEN_out, decoder_1_out0, decoder_1_out1, decoder_1_out2, decoder_1_out3, decoder_1_out4,
       decoder_1_out5, decoder_1_out6, decoder_1_out7;
  wire [7:0] REG3_q, REG4_q, REG5_q, REG6_q;

  Clock CLOCK_GEN (.out(CLOCK_GEN_out));
  Decoder #(.select(3)) decoder_1 (
    .out0(decoder_1_out0), .out1(decoder_1_out1), .out2(decoder_1_out2), .out3(decoder_1_out3),
    .out4(decoder_1_out4), .out5(decoder_1_out5), .out6(decoder_1_out6), .out7(decoder_1_out7),
    .sel(WriteReg), .en(WRITE));
  Register REG0 (.D(InputData), .en(decoder_1_out0), .clk(CLOCK_GEN_out), .Q(ARG0));  // open: clr
  Register REG1 (.D(InputData), .en(decoder_1_out1), .clk(CLOCK_GEN_out), .Q(ARG1));  // open: clr
  Register REG2 (.D(InputData), .en(decoder_1_out2), .clk(CLOCK_GEN_out), .Q(ARG2));  // open: clr
  Register REG3 (.D(InputData), .en(decoder_1_out3), .clk(CLOCK_GEN_out), .Q(REG3_q));  // open: clr
  Register REG4 (.D(InputData), .en(decoder_1_out4), .clk(CLOCK_GEN_out), .Q(REG4_q));  // open: clr
  Register REG5 (.D(InputData), .en(decoder_1_out5), .clk(CLOCK_GEN_out), .Q(REG5_q));  // open: clr
  Register REG6 (.D(InputData), .en(decoder_1_out6), .clk(CLOCK_GEN_out), .Q(REG6_q));  // open: clr
  Register REG7 (.D(InputData), .en(decoder_1_out7), .clk(CLOCK_GEN_out), .Q(RamAdress));  // open: clr
  Multiplexer #(.enable("true"), .select(3), .width(8)) multiplexer_1 (
    .in0(ARG0), .in1(ARG1), .in2(ARG2), .in3(REG3_q), .in4(REG4_q), .in5(REG5_q), .in6(REG6_q),
    .in7(RamAdress), .out(OutputData), .sel(ReadReg), .en(READ));

  // Notes on the sheet:
  //   READ: pull=down
endmodule

module ProgramCounter (
  input  Load,
  input  [7:0] Data,
  output [7:0] OutputData
);

  wire clock_1_out;
  wire [7:0] adder_1_out, multiplexer_1_out, register_1_q;

  Clock clock_1 (.out(clock_1_out));
  Register register_1 (.D(multiplexer_1_out), .en(clock_1_out), .clk(clock_1_out), .Q(register_1_q));  // open: clr
  Multiplexer #(.width(8)) multiplexer_1 (.in0(adder_1_out), .in1(Data), .out(multiplexer_1_out), .sel(Load));
  ROM rom_1 (.addr(register_1_q), .data(OutputData));
  Adder adder_1 (.a(8'h1), .b(register_1_q), .out(adder_1_out));  // open: cin, cout
  // Probe on OutputData

  // Notes on the sheet:
  //   Load: pull=down
  //   contents of rom_1 (hex, n*v repeats v):
  //   1 41 0 e0 42 0 e0 41 78 82
endmodule

module InstrDecoder (
  input  [7:0] INSTR,
  output Write,
  output [2:0] WriteAddr,
  output Read,
  output [2:0] ReadAddr,
  output [3:0] Const,
  output [1:0] OPCODE,
  output ALU_ACTIVE,
  output Conditional,
  output [7:0] JmpAdress,
  output LoadMem,
  output StoreMem
);

  wire decoder_1_out1, decoder_1_out3;
  wire [2:0] multiplexer_2_out;

  assign JmpAdress = {{2{1'b0}}, INSTR[5:0]};  // Bit_Extender bit_extender_1
  Decoder #(.enable("false"), .select(2)) decoder_1 (
    .out0(ALU_ACTIVE), .out1(decoder_1_out1), .out2(Conditional), .out3(decoder_1_out3), .sel(INSTR[7:6]));
  or or_1 (Write, decoder_1_out1, LoadMem, ALU_ACTIVE);
  Multiplexer #(.width(3)) multiplexer_1 (.in0(multiplexer_2_out), .in1(INSTR[4:2]), .out(WriteAddr), .sel(LoadMem));
  Multiplexer #(.width(3)) multiplexer_2 (.in0(INSTR[2:0]), .in1(3'b000), .out(multiplexer_2_out), .sel(ALU_ACTIVE));
  or or_2 (Read, decoder_1_out1, StoreMem);
  Decoder decoder_2 (.out0(LoadMem), .out1(StoreMem), .sel(INSTR[5]), .en(decoder_1_out3));
  Multiplexer #(.width(3)) multiplexer_3 (.in0(INSTR[5:3]), .in1(INSTR[4:2]), .out(ReadAddr), .sel(StoreMem));

  assign Const = INSTR[3:0];
  assign OPCODE = INSTR[5:4];

  // Notes on the sheet:
  //   ALU_ACTIVE: pull=down
  //   Conditional: pull=down
  //   LoadMem: pull=down
  //   StoreMem: pull=down
  //   JmpAdress: pull=down
endmodule
